# Fritzing sketch 2-3 (saved by Fritzing 1.0.5)
breadboards: 1

parts:
  Part1 = Arduino Uno (Rev3) - ICSP
  LED1 = LED - 3mm [color="Red (633nm)" current=0.030A package="3 mm [THT]"]
  R1 = Resistor [tolerance=±5% resistance=220 package="0402 [SMD]"]

nets (from the schematic view):
  N1: Part1.GND, LED1.cathode
  N2: Part1.D8, R1.Pin_1
  N3: LED1.anode, R1.Pin_0
